// Digital circuit ALU.dig as structural Verilog
// The Arithmetic Logic Unit (ALU) component, which can perform various operations on the provided operands, also determining the resulting flag values.
module ALU (
  input  [31:0] B,
  input  [31:0] A,
  input  [2:0] Opcode,
  output [31:0] Result,
  output Carry,
  output Overflow,
  output Negative,
  output Zero
);

  wire ADD_c_o, and_3_out, and_4_out, not_1_out, SUB_c_o, xnor_1_out, xor_2_out, xor_3_out, xor_4_out;
  wire [31:0] ADD_s, and_1_out, and_2_out, or_1_out, ROL_out, SUB_s, xor_1_out;

  Multiplexer #(.Selector_Bits(3), .Bits(32)) multiplexer_1 (
    .sel(Opcode), .in_0(or_1_out), .in_1(xor_1_out), .in_2(and_1_out), .in_3(and_2_out), .in_4({32{1'b0}}),
    .in_5(ROL_out), .in_6(ADD_s), .in_7(SUB_s), .out({Negative, Result[30:0]}));
  assign or_1_out = A | B;  // Or or_1, 32 bits wide
  assign xor_1_out = A ^ B;  // XOr xor_1, 32 bits wide
  assign and_1_out = A & B;  // And and_1, 32 bits wide
  assign and_2_out = A & ~B;  // And and_2, 32 bits wide
  BarrelShifter #(.Bits(32), .barrelShifterMode("rotate"), .barrelSigned("true")) ROL (
    .in(B), .shift(A[6:0]), .out(ROL_out));
  Add #(.Bits(32)) ADD (.a(A), .b(B), .c_i(1'b0), .s(ADD_s), .c_o(ADD_c_o));
  Sub #(.Bits(32)) SUB (.a(A), .b(B), .c_i(1'b0), .s(SUB_s), .c_o(SUB_c_o));
  not not_1 (not_1_out, SUB_c_o);
  Comparator #(.Signed("true"), .Bits(32)) comparator_1 (
    .a({Negative, Result[30:0]}), .b({32{1'b0}}), .eq(Zero));  // open: gt, lt
  xnor xnor_1 (xnor_1_out, B[31], A[31]);
  xor xor_2 (xor_2_out, Negative, B[31]);
  xor xor_3 (xor_3_out, Negative, A[31]);
  xor xor_4 (xor_4_out, B[31], A[31]);
  and and_3 (and_3_out, xnor_1_out, xor_3_out);
  and and_4 (and_4_out, xor_3_out, xor_4_out);
  Multiplexer #(.Selector_Bits(3)) multiplexer_2 (
    .sel(Opcode), .in_0(1'b0), .in_1(1'b0), .in_2(1'b0), .in_3(1'b0), .in_4(1'b0), .in_5(Result[0]),
    .in_6(ADD_c_o), .in_7(not_1_out), .out(Carry));
  Multiplexer #(.Selector_Bits(3)) multiplexer_3 (
    .sel(Opcode), .in_0(1'b0), .in_1(1'b0), .in_2(1'b0), .in_3(1'b0), .in_4(1'b0), .in_5(xor_2_out),
    .in_6(and_3_out), .in_7(and_4_out), .out(Overflow));

  assign Result[31] = Negative;

  // Notes on the sheet:
  //   B: The value of the ALU B operand.
  //   A: The value of the ALU A operand.
  //   Result: The resuling value, containing the value computed by the ALU.
  //   Carry: The resulting carry flag.
  //   Overflow: The resulting overflow flag.
  //   Negative: The resulting negative flag.
  //   Zero: The resulting zero flag.
  //   Opcode: The ALU opcode, which specifies the operation to perform.
endmodule

/* Test case Sub:
A B Opcode Result Carry Overflow Negative Zero

loop(i, 256)
    # determine random values for A and B inputs
    let a = random(1<<32);
    let b = random(1<<32);

    # compute expected Result
    let r = a + (~b & 0xffffffff) + 1;

    # determine expected flags
    let c = (r) >= (1<<32);
    let o = (((a>>31) & 1) != ((b>>31) & 1)) & (((a>>31) & 1) != ((r>>31) & 1));
    let n = (r>>31) & 1;
    let z = r=0;

    # perform subtraction, and then check Result and flags are as expected
    (a) (b) 7 (r) (c) (o) (n) (z)
end loop
*/

/* Test case Rol:
A B Opcode Result Carry Overflow Negative Zero

loop(i, 256)
    # determine random values for A and B inputs
    let a = random(1<<32);
    let b = random(1<<32);

    # compute expected Result
    let rot = a & 31;
    let r = (b << rot) | (b >> (32-rot));

    # determine expected flags
    let c = r & 1;
    let o = ((b>>31) & 1) != ((r>>31) & 1);
    let n = (r>>31) & 1;
    let z = r=0;

    # perform rotation, and then check Result and flags are as expected
    (a) (b) 5 (r) (c) (o) (n) (z)
end loop
*/
