// Digital circuit FlagRegisterBank.dig as structural Verilog
// The FlagRegisterBank component, which stores the current values of the overflow, negative, carry and zero flags.
module FlagRegisterBank (
  input  Clock,
  input  Carry_in,
  input  Overflow_in,
  input  Negative_in,
  input  Zero_in,
  input  SetFlag,
  output Carry_out,
  output Overflow_out,
  output Negative_out,
  output Zero_out
);

  Register Carry (.D(Carry_in), .C(Clock), .en(SetFlag), .Q(Carry_out));
  Register Overflow (.D(Overflow_in), .C(Clock), .en(SetFlag), .Q(Overflow_out));
  Register Negative (.D(Negative_in), .C(Clock), .en(SetFlag), .Q(Negative_out));
  Register Zero (.D(Zero_in), .C(Clock), .en(SetFlag), .Q(Zero_out));

  // Notes on the sheet:
  //   Carry_out: The current value of the stored carry flag.
  //   Overflow_out: The current value of the stored overflow flag.
  //   Negative_out: The current value of the stored negative flag.
  //   Zero_out: The current value of the stored zero flag.
  //   Carry_in
  //   Overflow_in
  //   Negative_in
  //   Zero_in
  //   Clock
  //   SetFlag
endmodule
