// Digital circuit InstructionDecoder.dig as structural Verilog
// The InstructionDecoder component, which serves as a hub to control many of the signals to other components. It implements both the fetch operation, and execution of machine code (including decoding).
module InstructionDecoder (
  input  [31:0] Instruction,
  input  Fetch,
  input  Execute,
  input  Clock,
  output Pop,
  output [3:0] Reg_dest,
  output [3:0] Reg_B,
  output [3:0] Reg_A,
  output [31:0] Constant,
  output UseConstant,
  output [2:0] Opcode,
  output [3:0] Condition,
  output SetFlag,
  output nWE,
  output nRE,
  output Halt
);

  wire and_9_out, and_12_out, ARITCons_eq, ARITnCons_eq, comparator_1_eq, decoder_1_out_0, decoder_1_out_1,
       decoder_1_out_2, decoder_1_out_3, decoder_1_out_4, decoder_1_out_5, decoder_1_out_6, HALT_eq,
       LOADHI_2_eq, LOADHI_eq, nor_1_out, or_1_out, or_2_out, or_3_out, or_4_out, or_6_out, POP_eq, PUSH_eq,
       READ_eq, WRITE_eq;
  wire [2:0] priorityencoder_1_num;
  wire [3:0] demultiplexer_1_out_1, demultiplexer_2_out_1, demultiplexer_3_out_1;
  wire [31:0] and_1_out, and_2_out, and_3_out, and_4_out, and_5_out, and_6_out, and_7_out, and_8_out,
       bitextender_1_out, IR_q, multiplexer_2_out;
  wire [31:4] multiplexer_1_out;

  Register #(.Bits(32)) IR (.D(Instruction), .C(Clock), .en(Fetch), .Q(IR_q));
  Multiplexer #(.Bits(32)) multiplexer_1 (
    .sel(Fetch), .in_0(IR_q), .in_1(32'h60040fff), .out({multiplexer_1_out, Condition}));
  assign and_1_out = {multiplexer_1_out, Condition} & 32'hfc0000f0;  // And and_1, 32 bits wide
  assign and_2_out = {multiplexer_1_out, Condition} & 32'hffff0ff0;  // And and_2, 32 bits wide
  assign and_3_out = {multiplexer_1_out, Condition} & 32'hfffffff0;  // And and_3, 32 bits wide
  assign and_4_out = {multiplexer_1_out, Condition} & 32'hfc00f000;  // And and_4, 32 bits wide
  assign and_5_out = {multiplexer_1_out, Condition} & 32'hffffff00;  // And and_5, 32 bits wide
  assign and_6_out = {multiplexer_1_out, Condition} & 32'hc0000000;  // And and_6, 32 bits wide
  assign and_7_out = {multiplexer_1_out, Condition} & 32'h87ff0000;  // And and_7, 32 bits wide
  assign and_8_out = {multiplexer_1_out, Condition} & 32'h8400f000;  // And and_8, 32 bits wide
  BitExtender #(.inputBits(10), .outputBits(32)) bitextender_1 (.in(multiplexer_1_out[25:16]), .out(bitextender_1_out));
  Comparator #(.Bits(32)) u_HALT (.a(and_3_out), .b(32'hfffffff0), .eq(HALT_eq));  // open: gt, lt
  Comparator #(.Bits(32)) READ (.a(and_4_out), .b(32'hc0000000), .eq(READ_eq));  // open: gt, lt
  Comparator #(.Bits(32)) WRITE (.a(and_1_out), .b(32'he0000000), .eq(WRITE_eq));  // open: gt, lt
  Comparator #(.Bits(32)) PUSH (.a(and_2_out), .b(32'hc4000ee0), .eq(PUSH_eq));  // open: gt, lt
  Comparator #(.Bits(32)) u_POP (.a(and_5_out), .b(32'hd0000e00), .eq(POP_eq));  // open: gt, lt
  Comparator #(.Bits(32)) LOADHI (.a(and_6_out), .b(32'h80000000), .eq(LOADHI_eq));  // open: gt, lt
  Comparator #(.Bits(32)) ARITnCons (.a(and_7_out), .b(32'h4000000), .eq(ARITnCons_eq));  // open: gt, lt
  Comparator #(.Bits(32)) ARITCons (.a(and_8_out), .b({32{1'b0}}), .eq(ARITCons_eq));  // open: gt, lt
  Multiplexer #(.Bits(32)) multiplexer_2 (
    .sel(LOADHI_2_eq), .in_0(bitextender_1_out), .in_1({multiplexer_1_out[29:8], {10{1'b0}}}),
    .out(multiplexer_2_out));
  or or_1 (or_1_out, ARITnCons_eq, ARITCons_eq);
  Comparator #(.Bits(4)) comparator_1 (.a(multiplexer_1_out[7:4]), .b(4'b1110), .eq(comparator_1_eq));  // open: gt, lt
  and and_9 (and_9_out, comparator_1_eq, decoder_1_out_5);
  PriorityEncoder #(.Selector_Bits(3)) priorityencoder_1 (
    .in0(1'b1), .in1(HALT_eq), .in2(READ_eq), .in3(WRITE_eq), .in4(PUSH_eq), .in5(POP_eq), .in6(LOADHI_eq),
    .in7(or_1_out), .num(priorityencoder_1_num));  // open: any
  Comparator #(.Bits(3)) LOADHI_2 (.a(3'b110), .b(priorityencoder_1_num), .eq(LOADHI_2_eq));  // open: gt, lt
  Decoder #(.Selector_Bits(3)) decoder_1 (
    .sel(priorityencoder_1_num), .out_0(decoder_1_out_0), .out_1(decoder_1_out_1), .out_2(decoder_1_out_2),
    .out_3(decoder_1_out_3), .out_4(decoder_1_out_4), .out_5(decoder_1_out_5), .out_6(decoder_1_out_6));  // open: out_7
  nor nor_1 (nor_1_out, multiplexer_1_out[26], decoder_1_out_5);
  or or_2 (or_2_out, and_9_out, decoder_1_out_0, decoder_1_out_1);
  or or_3 (or_3_out, decoder_1_out_2, decoder_1_out_5);
  and and_10 (SetFlag, ~decoder_1_out_1, multiplexer_1_out[27]);  // And
  or or_4 (or_4_out, decoder_1_out_4, decoder_1_out_3);
  Demultiplexer #(.Bits(4)) demultiplexer_1 (
    .sel(and_9_out), .in(multiplexer_1_out[7:4]), .out_0(Reg_dest), .out_1(demultiplexer_1_out_1));
  Demultiplexer #(.Bits(4)) demultiplexer_2 (
    .sel(decoder_1_out_6), .in(multiplexer_1_out[11:8]), .out_0(Reg_B), .out_1(demultiplexer_2_out_1));
  and and_11 (Halt, or_2_out, Execute);
  or or_5 (UseConstant, decoder_1_out_6, nor_1_out);
  or or_6 (or_6_out, decoder_1_out_3, decoder_1_out_4, decoder_1_out_6);
  Multiplexer #(.Bits(32)) multiplexer_3 (
    .sel(decoder_1_out_5), .in_0(multiplexer_2_out), .in_1(32'hfffffffc), .out(Constant));
  and and_12 (and_12_out, or_3_out, Execute);
  Demultiplexer #(.Bits(4)) demultiplexer_3 (
    .sel(decoder_1_out_6), .in(multiplexer_1_out[15:12]), .out_0(Reg_A), .out_1(demultiplexer_3_out_1));
  and and_13 (Pop, decoder_1_out_5, Execute);
  nand nand_1 (nWE, or_4_out, Execute);
  nor nor_2 (nRE, and_12_out, Fetch);
  Multiplexer #(.Bits(3)) multiplexer_4 (.sel(or_6_out), .in_0(multiplexer_1_out[30:28]), .in_1(3'b110), .out(Opcode));
  // also tied to GND on the sheet: {demultiplexer_2_out_1[0], demultiplexer_2_out_1[1], demultiplexer_2_out_1[2], demultiplexer_2_out_1[3], demultiplexer_1_out_1[0], demultiplexer_1_out_1[1], demultiplexer_1_out_1[2], demultiplexer_1_out_1[3], demultiplexer_3_out_1[0], demultiplexer_3_out_1[1], demultiplexer_3_out_1[2], demultiplexer_3_out_1[3]}

  // Notes on the sheet:
  //   Instruction: The instruction machine code input. If the CPU is in the fetch phase and a rising clock signal occurs, this machine code is stored in the internal instruction register (IR), so that it can be decoded and executed.
  //   Reg_dest: Destination register output, which determines the register that should store the result of a data operation. A data operation is either an ALU computation, or a read from an external device, such as RAM.
  //   Reg_B: B register output, which determines the register to be used for the second operand.
  //   Reg_A: A register output, which determines the register to be used for the first operand.
  //   UseConstant: The bit that chooses to use Reg_A or a constant to input A of he ALU
  //   Condition: Instruction condition output, which contains the condition under which the instruction should be executed.
  //   nWE: Not write enable
  //   nRE: not read enable
  //   condition
  //   This part checks if the instruction is valid
  //   returns 1 for HALT, 2 for READ, etc
endmodule
