// Digital circuit RegSP.dig as structural Verilog
// Wrapper around a register component with an additional pop input, which if set will increment the value stored in the register by 4 on a rising clock edge.
module RegSP (
  input  [31:0] D,
  input  C,
  input  en,
  input  pop,
  output [31:0] Q
);

  wire not_1_out, or_1_out;
  wire [31:0] add_1_s, multiplexer_1_out;

  Add #(.Bits(32)) add_1 (.a(Q), .b(32'h4), .c_i(1'b0), .s(add_1_s));  // open: c_o
  Multiplexer #(.Bits(32)) multiplexer_1 (.sel(not_1_out), .in_0(add_1_s), .in_1(D), .out(multiplexer_1_out));
  not not_1 (not_1_out, pop);
  or or_1 (or_1_out, pop, en);
  Register #(.Bits(32)) R14 (.D(multiplexer_1_out), .C(C), .en(or_1_out), .Q(Q));
endmodule
