// Digital circuit RegisterBank.dig as structural Verilog
// The RegisterBank component, which contains and manages all the CPU registers (except the flag registers).
module RegisterBank (
  input  [31:0] Data_in,
  input  Pop,
  input  [3:0] Reg_dest,
  input  [3:0] Reg_B,
  input  [3:0] Reg_A,
  input  Clock,
  output [31:0] Data_B,
  output [31:0] Data_A
);

  wire decoder_1_out_1, decoder_1_out_2, decoder_1_out_3, decoder_1_out_4, decoder_1_out_5, decoder_1_out_6,
       decoder_1_out_7, decoder_1_out_8, decoder_1_out_9, decoder_1_out_10, decoder_1_out_11,
       decoder_1_out_12, decoder_1_out_13, decoder_1_out_14, decoder_1_out_15;
  wire [31:0] R0_q, R1_q, R2_q, R3_q, R4_q, R5_q, R6_q, R7_q, R8_q, R9_q, R10_q, R11_q, R12_q, R13_q, R14_q,
       R15_q;

  Register #(.Bits(32)) R12 (.D(Data_in), .C(Clock), .en(decoder_1_out_12), .Q(R12_q));
  Register #(.Bits(32)) R13 (.D(Data_in), .C(Clock), .en(decoder_1_out_13), .Q(R13_q));
  RegSP R14 (.D(Data_in), .C(Clock), .en(decoder_1_out_14), .pop(Pop), .Q(R14_q));
  Register #(.Bits(32), .isProgramCounter("true")) R15 (.D(Data_in), .C(Clock), .en(decoder_1_out_15), .Q(R15_q));
  Decoder #(.Selector_Bits(4)) decoder_1 (
    .sel(Reg_dest), .out_1(decoder_1_out_1), .out_2(decoder_1_out_2), .out_3(decoder_1_out_3),
    .out_4(decoder_1_out_4), .out_5(decoder_1_out_5), .out_6(decoder_1_out_6), .out_7(decoder_1_out_7),
    .out_8(decoder_1_out_8), .out_9(decoder_1_out_9), .out_10(decoder_1_out_10), .out_11(decoder_1_out_11),
    .out_12(decoder_1_out_12), .out_13(decoder_1_out_13), .out_14(decoder_1_out_14), .out_15(decoder_1_out_15));  // open: out_0
  Register #(.Bits(32)) R8 (.D(Data_in), .C(Clock), .en(decoder_1_out_8), .Q(R8_q));
  Register #(.Bits(32)) R9 (.D(Data_in), .C(Clock), .en(decoder_1_out_9), .Q(R9_q));
  Register #(.Bits(32)) R10 (.D(Data_in), .C(Clock), .en(decoder_1_out_10), .Q(R10_q));
  Register #(.Bits(32)) R11 (.D(Data_in), .C(Clock), .en(decoder_1_out_11), .Q(R11_q));
  Register #(.Bits(32)) R4 (.D(Data_in), .C(Clock), .en(decoder_1_out_4), .Q(R4_q));
  Register #(.Bits(32)) R5 (.D(Data_in), .C(Clock), .en(decoder_1_out_5), .Q(R5_q));
  Register #(.Bits(32)) R6 (.D(Data_in), .C(Clock), .en(decoder_1_out_6), .Q(R6_q));
  Register #(.Bits(32)) R7 (.D(Data_in), .C(Clock), .en(decoder_1_out_7), .Q(R7_q));
  Register #(.Bits(32)) R0 (.D({32{1'b0}}), .C(1'b0), .en(1'b0), .Q(R0_q));
  Register #(.Bits(32)) R1 (.D(Data_in), .C(Clock), .en(decoder_1_out_1), .Q(R1_q));
  Register #(.Bits(32)) R2 (.D(Data_in), .C(Clock), .en(decoder_1_out_2), .Q(R2_q));
  Register #(.Bits(32)) R3 (.D(Data_in), .C(Clock), .en(decoder_1_out_3), .Q(R3_q));
  Multiplexer #(.Selector_Bits(4), .Bits(32)) multiplexer_1 (
    .sel(Reg_A), .in_0(R0_q), .in_1(R1_q), .in_2(R2_q), .in_3(R3_q), .in_4(R4_q), .in_5(R5_q), .in_6(R6_q),
    .in_7(R7_q), .in_8(R8_q), .in_9(R9_q), .in_10(R10_q), .in_11(R11_q), .in_12(R12_q), .in_13(R13_q),
    .in_14(R14_q), .in_15(R15_q), .out(Data_A));
  Multiplexer #(.Selector_Bits(4), .Bits(32)) multiplexer_2 (
    .sel(Reg_B), .in_0(R0_q), .in_1(R1_q), .in_2(R2_q), .in_3(R3_q), .in_4(R4_q), .in_5(R5_q), .in_6(R6_q),
    .in_7(R7_q), .in_8(R8_q), .in_9(R9_q), .in_10(R10_q), .in_11(R11_q), .in_12(R12_q), .in_13(R13_q),
    .in_14(R14_q), .in_15(R15_q), .out(Data_B));

  // Notes on the sheet:
  //   Data_in: Data input pin, containing the data word to be stored in a register.
  //   Pop: Input pin that signals a pop instruction is being executed. If this pin is high -and a rising clock signal occurs- the value in register R14 (SP) is increment by 4.
  //   Reg_dest: Destination register. This input pin selects the register to store the contents of the data input pin in if a rising clock edge occurs. Writes to register R0 are discared.
  //   Reg_B: Register B input pin that selects which register's content should be set on the Data_B output pin.
  //   Reg_A: Register A input pin that selects which register's content should be set on the Data_A output pin.
  //   Data_B: Output pin that contains the contents of the register selected by the Reg_B input pin.
  //   Data_A: Output pin that contains the contents of the register selected by the Reg_A input pin.
endmodule
