// Digital circuit Tester.dig as structural Verilog
// The Tester component, which given a condition and set of flags will test whether the condition was met or not.
module Tester (
  input  [3:0] Condition,
  input  Carry,
  input  Overflow,
  input  Negative,
  input  Zero,
  output TestSucceeds
);

  wire and_1_out, and_2_out, not_1_out, not_2_out, not_3_out, not_4_out, not_5_out, or_1_out, or_2_out,
       xnor_1_out;

  not not_1 (not_1_out, Zero);
  not not_2 (not_2_out, Carry);
  not not_3 (not_3_out, Negative);
  not not_4 (not_4_out, Overflow);
  and and_1 (and_1_out, Carry, not_1_out);
  or or_1 (or_1_out, Zero, not_2_out);
  xnor xnor_1 (xnor_1_out, Negative, Overflow);
  not not_5 (not_5_out, xnor_1_out);
  and and_2 (and_2_out, xnor_1_out, not_1_out);
  or or_2 (or_2_out, not_5_out, Zero);
  Multiplexer #(.Selector_Bits(4)) multiplexer_1 (
    .sel(Condition), .in_0(Zero), .in_1(not_1_out), .in_2(Carry), .in_3(not_2_out), .in_4(Negative),
    .in_5(not_3_out), .in_6(Overflow), .in_7(not_4_out), .in_8(and_1_out), .in_9(or_1_out),
    .in_10(xnor_1_out), .in_11(not_5_out), .in_12(and_2_out), .in_13(or_2_out), .in_14(1'b0), .in_15(1'b1),
    .out(TestSucceeds));

  // Notes on the sheet:
  //   TestSucceeds: Determines whether the test succeeded (indicating the instruction should be executed), or failed (indicating the instruction should be skipped).
endmodule

/* Test case:
Condition Carry Overflow Negative Zero TestSucceeds

loop(c, 2)
  loop(o, 2)
    loop(n, 2)
      loop(z, 2)
        0b0100 (c) (o) (n) (z) (n)
        0b1000 (c) (o) (n) (z) (c & !z)
        0b1100 (c) (o) (n) (z) ((n = o) & !z)
        0b1101 (c) (o) (n) (z) ((n != o) | z)
        0b1111 (c) (o) (n) (z) 1
      end loop
    end loop
  end loop
end loop
*/
